# Fritzing sketch wolverineflasher (saved by Fritzing 0.9.3b)
breadboards: 1

parts:
  Wolverine_Flasher = Arduino Nano (Rev3.0)
  R1 = Resistor [tolerance=±5% resistance=220 package=THT]
  R2 = Resistor [tolerance=±5% resistance=220 package=THT]
  Yellow_LED = LED - 5mm [color="Red (633nm)" package="5 mm [THT]"]
  Blue_LED = LED - 5mm [color="Red (633nm)" package="5 mm [THT]"]

nets:
  N1: Wolverine_Flasher.GND, Yellow_LED.cathode, Blue_LED.cathode
  N2: Wolverine_Flasher.D2, R1.Pin_0
  N3: Wolverine_Flasher.D3, R2.Pin_0
  N4: R1.Pin_1, Blue_LED.anode
  N5: R2.Pin_1, Yellow_LED.anode
